# Fritzing sketch USBtoC64-1.0 (saved by Fritzing 1.0.2b)
circuit board: 3.08899cm x 3.18237cm
breadboards: 1

parts:
  X1 = DB9 Connector [package=db9]
  A2 = ESP32-S3 supermini
  Q1 = NPN-Transistor [package="TO92 [THT]"]
  1K = Resistor [tolerance=±5% power=0.25W resistance=220 package=THT]
  1K_2 = Resistor [tolerance=±5% power=0.25W resistance=220 package=THT]
  150 = Resistor [tolerance=±5% power=0.25W resistance=220 package=THT]
  150_2 = Resistor [tolerance=±5% power=0.25W resistance=220 package=THT]
  D1 = Diode [package=diode-1n4148]
  D2 = Diode [package=diode-1n4148]
  S1 = Toggle Switch [package=THT]

nets:
  N1: X1.1, A2.Pin_33
  N2: X1.2, A2.Pin_34
  N3: X1.3, A2.Pin_35
  N4: X1.4, A2.Pin_36
  N5: X1.5, D1.C
  N6: X1.6, A2.Pin_32
  N7: X1.7, A2.Pin_3, 1K_2.Pin_0
  N8: X1.8, A2.Pin_4, Q1.C, S1.L2
  N9: X1.9, 1K.Pin_0, D2.C
  N10: A2.Pin_6, Q1.E, 1K_2.Pin_1
  N11: A2.Pin_7, S1.COM
  N12: A2.Pin_9, 150_2.Pin_1
  N13: A2.Pin_11, 150.Pin_0
  N14: Q1.B, 1K.Pin_1
  N15: 150.Pin_1, D1.A
  N16: 150_2.Pin_0, D2.A

notes:
  mode
  joystick
  mouse
  USB to C64 rev. 1.1
  Emanuele Laface

custom parts:
  ESP32-S3 supermini: Esp32-S3 Development board ESP32 SuperMini development board ESP32 Development board WiFi Bluetooth.
