# Fritzing sketch USBtoC64-4.0 (saved by Fritzing 1.0.2b)
circuit board: 2.61568cm x 1.97239cm
breadboards: 1

parts:
  Pad1 = Pad [width=2.833411121253748 height=1.6186319467511874 connect=center]
  Pad2 = Pad [width=2.833411121253748 height=1.6186319467511874 connect=center]
  Pad3 = Pad [width=2.833411121253748 height=1.6186319467511874 connect=center]
  Pad4 = Pad [width=2.833411121253748 height=1.6186319467511874 connect=center]
  Pad5 = Pad [width=2.833411121253748 height=1.6186319467511874 connect=center]
  Pad8 = Pad [width=2.833411121253748 height=1.6186319467511874 connect=center]
  Pad9 = Pad [width=2.833411121253748 height=1.6186319467511874 connect=center]
  Pad7 = Pad [width=2.833411121253748 height=1.6186319467511874 connect=center]
  Pad6 = Pad [width=2.833411121253748 height=1.6186319467511874 connect=center]
  Pad10 = Pad [width=1.98 height=2.5 connect=center]
  Pad11 = Pad [width=1.98 height=2.5 connect=center]
  Pad12 = Pad [width=1.98 height=2.5 connect=center]  # not connected
  Pad13 = Pad [width=1.98 height=2.5 connect=center]
  Pad14 = Pad [width=1.98 height=2.5 connect=center]  # not connected
  Pad15 = Pad [width=1.98 height=2.5 connect=center]  # not connected
  Pad16 = Pad [width=1.98 height=2.5 connect=center]
  Pad17 = Pad [width=1.98 height=2.5 connect=center]  # not connected
  Pad18 = Pad [width=1.98 height=2.5 connect=center]
  Pad19 = Pad [width=1.98 height=2.5 connect=center]  # not connected
  Pad20 = Pad [width=1.98 height=2.5 connect=center]
  Pad21 = Pad [width=1.98 height=2.5 connect=center]
  Pad22 = Pad [width=1.98 height=2.5 connect=center]
  Pad23 = Pad [width=1.98 height=2.5 connect=center]  # not connected
  Pad24 = Pad [width=1.98 height=2.5 connect=center]  # not connected
  Pad25 = Pad [width=1.98 height=2.5 connect=center]
  Pad26 = Pad [width=1.98 height=2.5 connect=center]
  Pad27 = Pad [width=1.98 height=2.5 connect=center]
  1K = Resistor [tolerance=±5% resistance=220 package="0805 [SMD]"]
  1K_2 = Resistor [tolerance=±5% resistance=220 package="0805 [SMD]"]
  150 = Resistor [tolerance=±5% resistance=220 package="0805 [SMD]"]
  150_2 = Resistor [tolerance=±5% resistance=220 package="0805 [SMD]"]
  5_1K = Resistor [tolerance=±5% resistance=220 package="0805 [SMD]"]
  Q1 = NPN-Transistor [package="SOT-23 [SMD]"]
  D1 = Rectifier Diode SOD-123F [package="SOD-123F [SMD]"]
  D2 = Rectifier Diode SOD-123F [package="SOD-123F [SMD]"]
  Pad28 = Pad [width=0.45 height=1 connect=center]
  Pad29 = Pad [width=0.45 height=1 connect=center]
  Pad30 = Pad [width=0.45 height=1 connect=center]  # not connected
  Pad31 = Pad [width=0.45 height=0.6 connect=center]  # not connected
  Pad32 = Pad [width=0.45 height=0.6 connect=center]  # not connected
  Pad33 = Pad [width=0.45 height=0.6 connect=center]  # not connected
  Pad34 = Pad [width=0.45 height=0.6 connect=center]  # not connected

nets:
  N1: Pad1.pad, D2.cathode
  N2: Pad2.pad, Pad27.pad
  N3: Pad3.pad, Pad22.pad
  N4: Pad4.pad, Pad20.pad
  N5: Pad5.pad, Pad26.pad
  N6: Pad8.pad, Pad10.pad, 1K.Pin_1, 5_1K.Pin_1
  N7: Pad9.pad, Pad21.pad
  N8: Pad7.pad, Pad11.pad, Q1.2, Pad29.pad
  N9: Pad6.pad, 1K_2.Pin_0, 5_1K.Pin_0, D1.cathode
  N10: Pad13.pad, 1K.Pin_0, Q1.1
  N11: Pad16.pad, 150_2.Pin_1
  N12: Pad18.pad, 150.Pin_1
  N13: Pad25.pad, Pad28.pad
  N14: 1K_2.Pin_1, Q1.0
  N15: 150.Pin_0, D2.anode
  N16: 150_2.Pin_0, D1.anode

notes:
  4.0
  E.L.

custom parts:
  Rectifier Diode SOD-123F: A smd rectifier diode
