# Fritzing sketch USBtoC64-THT-3.2 (saved by Fritzing 1.0.2b)
circuit board: 2.95303cm x 1.98307cm
breadboards: 1

parts:
  Q1 = NPN-Transistor [package="TO92 [THT]"]
  1K = Resistor [tolerance=±5% power=0.25W resistance=220 package=THT]
  1K_2 = Resistor [tolerance=±5% power=0.25W resistance=220 package=THT]
  150 = Resistor [tolerance=±5% power=0.25W resistance=220 package=THT]
  150_2 = Resistor [tolerance=±5% power=0.25W resistance=220 package=THT]
  D1 = Diode [package=diode-1n4148]
  D2 = Diode [package=diode-1n4148]
  S1 = Toggle Switch [package=THT]
  A2 = ESP32-S3 supermini
  Pad1 = Pad [width=2.833411121253748 height=1.6186319467511874 connect=center]
  Pad2 = Pad [width=2.833411121253748 height=1.6186319467511874 connect=center]
  Pad3 = Pad [width=2.833411121253748 height=1.6186319467511874 connect=center]
  Pad4 = Pad [width=2.833411121253748 height=1.6186319467511874 connect=center]
  Pad5 = Pad [width=2.833411121253748 height=1.6186319467511874 connect=center]
  Pad8 = Pad [width=2.833411121253748 height=1.6186319467511874 connect=center]
  Pad9 = Pad [width=2.833411121253748 height=1.6186319467511874 connect=center]
  Pad7 = Pad [width=2.833411121253748 height=1.6186319467511874 connect=center]
  Pad6 = Pad [width=2.833411121253748 height=1.6186319467511874 connect=center]
  5_1k = Resistor [tolerance=±5% power=0.25W resistance=220 package=THT]

nets:
  N1: Q1.E, 1K_2.Pin_1, A2.Pin_6
  N2: Q1.B, 1K.Pin_1
  N3: Q1.C, S1.L2, A2.Pin_4, Pad7.pad
  N4: 1K.Pin_0, D2.C, A2.Pin_10, Pad6.pad, 5_1k.Pin_0
  N5: 1K_2.Pin_0, A2.Pin_3, Pad8.pad, 5_1k.Pin_1
  N6: 150.Pin_0, A2.Pin_11
  N7: 150.Pin_1, D1.A
  N8: 150_2.Pin_0, D2.A
  N9: 150_2.Pin_1, A2.Pin_9
  N10: D1.C, A2.Pin_8, Pad1.pad
  N11: S1.COM, A2.Pin_38
  N12: A2.Pin_32, Pad9.pad
  N13: A2.Pin_33, Pad5.pad
  N14: A2.Pin_34, Pad4.pad
  N15: A2.Pin_35, Pad3.pad
  N16: A2.Pin_36, Pad2.pad

notes:
  3.2
  J
  M
  E.L.

custom parts:
  ESP32-S3 supermini: Esp32-S3 Development board ESP32 SuperMini development board ESP32 Development board WiFi Bluetooth.
