# Fritzing sketch USBtoC64 (saved by Fritzing 1.0.2b)
circuit board: 3.10531cm x 1.97483cm
breadboards: 1

parts:
  X1 = DB9 Connector [package=db9]
  Q1 = NPN-Transistor [package="TO92 [THT]"]
  1K = Resistor [tolerance=±5% power=0.25W resistance=220 package=THT]
  1K_2 = Resistor [tolerance=±5% power=0.25W resistance=220 package=THT]
  150 = Resistor [tolerance=±5% power=0.25W resistance=220 package=THT]
  150_2 = Resistor [tolerance=±5% power=0.25W resistance=220 package=THT]
  D1 = Diode [package=diode-1n4148]
  D2 = Diode [package=diode-1n4148]
  S1 = Toggle Switch [package=THT]
  A2 = ESP32-S3 supermini

nets:
  N1: X1.1, A2.Pin_33
  N2: X1.2, A2.Pin_34
  N3: X1.3, A2.Pin_35
  N4: X1.4, A2.Pin_36
  N5: X1.5, D1.C
  N6: X1.6, A2.Pin_32
  N7: X1.7, 1K_2.Pin_0, A2.Pin_3
  N8: X1.8, Q1.C, S1.L2, A2.Pin_4
  N9: X1.9, 1K.Pin_0, D2.C
  N10: Q1.E, 1K_2.Pin_1, A2.Pin_6
  N11: Q1.B, 1K.Pin_1
  N12: 150.Pin_0, A2.Pin_11
  N13: 150.Pin_1, D1.A
  N14: 150_2.Pin_0, D2.A
  N15: 150_2.Pin_1, A2.Pin_9
  N16: S1.COM, A2.Pin_38

notes:
  USBtoC64 v2.1

custom parts:
  ESP32-S3 supermini: Esp32-S3 Development board ESP32 SuperMini development board ESP32 Development board WiFi Bluetooth.
